# Fritzing sketch trumphead (saved by Fritzing 0.9.3b)
breadboards: 1

parts:
  Part1 = Arduino Uno (Rev3)
  Flow_Meter = DS18B20 1-Wire Temperature Sensor [part_number=DS18B20]
  LED1 = RGB LED (com. cathode, rgb) [package="5 mm [THT]"]
  LED2 = RGB LED (com. cathode, rgb) [package="5 mm [THT]"]

nets:
  N1: Part1.D2, Flow_Meter.DQ
  N2: Part1.D5_PWM, LED1.red_anode
  5V: Part1.5V, Flow_Meter.VDD, LED1.common_cathode, LED2.common_cathode
  GND: Part1.GND, Flow_Meter.GND, LED1.green_anode, LED2.green_anode
  N3: LED1.blue_anode, LED2.red_anode
